# Fritzing sketch rotaryKey (saved by Fritzing 0.9.3b)
breadboards: 1

parts:
  R1 = Rotary Potentiometer (Large) [maximum_resistance=100kΩ package=THT]
  S3 = Momentary Switch [package=ksa_sealed_tac_switch]
  Part1 = Arduino Uno (Rev3)
  R2 = Resistor [tolerance=±5% resistance=10k package="1206 [SMD]"]
  R3 = Resistor [tolerance=±5% resistance=10k package="1206 [SMD]"]
  R4 = Resistor [tolerance=±5% resistance=10k package="1206 [SMD]"]
  S4 = Momentary Switch [package=ksa_sealed_tac_switch]
  S5 = Momentary Switch [package=ksa_sealed_tac_switch]

nets:
  N1: R1.leg1, S3.2, Part1.3V3, S4.2, S5.2
  N2: R1.wiper, Part1.A0
  N3: R1.leg2, Part1.GND, R2.Pin_1, R3.Pin_1, R4.Pin_1
  N4: S3.3, Part1.D2, R2.Pin_0
  N5: Part1.D3_PWM, R3.Pin_0, S4.3
  N6: Part1.D4, R4.Pin_0, S5.3
